# Fritzing sketch clock (saved by Fritzing 0.9.6b)
breadboards: 1

parts:
  R1 = Resistor [tolerance=±5% power=0.25 resistance=100 package=THT]
  A1 = Waveshare rp2040-zero tht [package=THT]
  VCC1 = 4 x AAA Battery Mount
  L2 = Inductor [package="400 mil [THT]"]

nets:
  N1: R1.Pin_0, A1.Pin_9
  N2: R1.Pin_1, L2.pin_0
  N3: A1.Pin_1, VCC1.+
  N4: A1.Pin_2, VCC1.-
  N5: A1.Pin_8, L2.pin_1

notes:
  .

custom parts:
  Waveshare rp2040-zero tht: .RP2040-Zero, A Low-Cost, High-Performance Pico-Like MCU Board Based On Raspberry Pi Microcontroller RP2040. This varant is THT without the extra connections.
